# Fritzing sketch thermistor (saved by Fritzing 1.0.3b)
breadboards: 1

parts:
  Part1 = Arduino Uno (Rev3)
  R1 = Temperature Sensor (Thermistor) [thermistor_type=NTC package=THT]
  R2 = Resistor [tolerance=±5% power=0.25W resistance=220 package=THT]
  LED1 = LED - 5mm [color="Red (633nm)" current=0.030A package="5 mm [THT]"]

nets:
  N1: Part1.5V, R1.pin_1
  N2: Part1.GND, LED1.cathode
  N3: R1.pin_0, R2.Pin_0
  N4: R2.Pin_1, LED1.anode
