# Fritzing sketch dimmable_LED (saved by Fritzing 1.0.3b)
breadboards: 1

parts:
  Part1 = Arduino Uno (Rev3)
  R2 = Rotary Potentiometer (Small) [maximum_resistance=10kΩ knob_status=50% power=0.5W package=THT]
  LED1 = LED - 5mm [color="Red (633nm)" current=0.030A package="5 mm [THT]"]

nets:
  N1: Part1.A5/SCL, R2.wiper, LED1.anode
  N2: Part1.GND, R2.leg1, LED1.cathode
  N3: Part1.5V, R2.leg2
