# Fritzing sketch photoresistor (saved by Fritzing 1.0.3b)
breadboards: 1

parts:
  Part1 = Arduino Uno (Rev3)
  R1 = Resistor [tolerance=±5% power=0.25W resistance=220 package=THT]
  LED1 = LED - 5mm [color="Red (633nm)" current=0.030A package="5 mm [THT]"]
  R2 = PHOTOCELL [package=photocell-kit]

nets:
  N1: Part1.GND, LED1.cathode
  N2: Part1.5V, R2.P$1
  N3: R1.Pin_0, R2.P$2
  N4: R1.Pin_1, LED1.anode
