# Fritzing sketch push_btn (saved by Fritzing 1.0.3b)
breadboards: 1

parts:
  S1 = Pushbutton [package="[THT]"]
  Part1 = Arduino Uno (Rev3)
  R1 = Resistor [tolerance=±5% power=0.25W resistance=220 package=THT]
  LED1 = LED - 5mm [color="Red (633nm)" current=0.030A package="5 mm [THT]"]

nets:
  N1: S1.Pin_1, S1.Pin_2, Part1.5V
  N2: S1.Pin_3, S1.Pin_4, R1.Pin_1
  N3: Part1.GND, LED1.cathode
  N4: R1.Pin_0, LED1.anode
