# Fritzing sketch static_LED (saved by Fritzing 1.0.3b)
breadboards: 1

parts:
  Part1 = Arduino Uno (Rev3)
  LED1 = LED - 5mm [color="Red (633nm)" current=0.030A package="5 mm [THT]"]
  R1 = Resistor [tolerance=±5% power=0.25W resistance=220 package=THT]
  VCC1 = Battery block 9V [internal_resistance=0.1Ω]  # not connected

nets:
  N1: Part1.5V, R1.Pin_1
  N2: Part1.GND, LED1.cathode
  N3: LED1.anode, R1.Pin_0

// code stored in the sketch: Untitled.ino
int ledPin = 8;      // select the pin for the LED

void setup() {
  // declare the ledPin as an OUTPUT:
  pinMode(ledPin, OUTPUT);
}

void loop() {
  // turn the ledPin on
  digitalWrite(ledPin, HIGH);
  // stop the program for <sensorValue> milliseconds:
  delay(1000);
  // turn the ledPin off:
  digitalWrite(ledPin, LOW);
  // stop the program for <sensorValue> milliseconds:
  delay(1000);
}
