# Fritzing sketch traffic_light (saved by Fritzing 1.0.3b)
breadboards: 1

parts:
  Part1 = Arduino Uno (Rev3)
  LED1 = LED - 5mm [color="Green (555nm)" current=0.030A package="5 mm [THT]"]
  LED2 = LED - 5mm [color="Yellow (592nm)" current=0.030A package="5 mm [THT]"]
  LED3 = LED - 5mm [color="Red (633nm)" current=0.030A package="5 mm [THT]"]
  R4 = Resistor [tolerance=±5% power=0.25W resistance=220 package=THT]
  R6 = Resistor [tolerance=±5% power=0.25W resistance=220 package=THT]
  R5 = Resistor [tolerance=±5% power=0.25W resistance=220 package=THT]

nets:
  N1: Part1.D8, R5.Pin_1
  N2: Part1.D12/MISO, R4.Pin_1
  N3: Part1.GND, LED1.cathode, LED2.cathode, LED3.cathode
  N4: Part1.D2, R6.Pin_1
  N5: LED1.anode, R4.Pin_0
  N6: LED2.anode, R5.Pin_0
  N7: LED3.anode, R6.Pin_0
